# Fritzing sketch Untitled Sketch 2 (saved by Fritzing 0.9.3b)
breadboards: 1

parts:
  Q1 = NPN-Transistor [part_number=BC237 package="TO92 [THT]"]
  R1 = Resistor [tolerance=±5% resistance=2.2k package=THT]
  LED1 = smd LED [color="White (8000K)" package="1206 [SMD]"]  # not connected
  LED2 = smd LED [color="White (8000K)" package="1206 [SMD]"]  # not connected
  LED3 = smd LED [color="White (8000K)" package="1206 [SMD]"]  # not connected
  LED4 = smd LED [color="White (8000K)" package="1206 [SMD]"]  # not connected
  LED5 = smd LED [color="White (8000K)" package="1206 [SMD]"]  # not connected
  LED6 = smd LED [color="White (8000K)" package="1206 [SMD]"]  # not connected
  Q2 = NPN-Transistor [part_number=BC237 package="TO92 [THT]"]  # not connected
  R2 = Resistor [tolerance=±5% resistance=2.2k package=THT]
  LED7 = smd LED [color="White (8000K)" package="1206 [SMD]"]  # not connected
  LED9 = smd LED [color="White (8000K)" package="1206 [SMD]"]  # not connected
  LED10 = smd LED [color="White (8000K)" package="1206 [SMD]"]  # not connected
  LED11 = smd LED [color="White (8000K)" package="1206 [SMD]"]  # not connected
  LED12 = smd LED [color="White (8000K)" package="1206 [SMD]"]  # not connected
  Q3 = NPN-Transistor [part_number=BC237 package="TO92 [THT]"]  # not connected
  R3 = Resistor [tolerance=±5% resistance=2.2k package=THT]
  LED13 = smd LED [color="White (8000K)" package="1206 [SMD]"]  # not connected
  LED14 = smd LED [color="White (8000K)" package="1206 [SMD]"]  # not connected
  LED15 = smd LED [color="White (8000K)" package="1206 [SMD]"]  # not connected
  LED16 = smd LED [color="White (8000K)" package="1206 [SMD]"]  # not connected
  LED17 = smd LED [color="White (8000K)" package="1206 [SMD]"]  # not connected
  LED18 = smd LED [color="White (8000K)" package="1206 [SMD]"]  # not connected
  12V_battery = Battery Holders [package=lipo-1100mAh]
  LED19 = smd LED [color="White (8000K)" package="1206 [SMD]"]  # not connected
  LED20 = smd LED [color="White (8000K)" package="1206 [SMD]"]  # not connected
  LED21 = smd LED [color="White (8000K)" package="1206 [SMD]"]  # not connected
  LED22 = smd LED [color="White (8000K)" package="1206 [SMD]"]  # not connected
  LED23 = smd LED [color="White (8000K)" package="1206 [SMD]"]  # not connected
  LED24 = smd LED [color="White (8000K)" package="1206 [SMD]"]
  LED25 = smd LED [color="White (8000K)" package="1206 [SMD]"]  # not connected
  ESP82266_module = Gizwits WiFi Witty ESP-12F

nets:
  N1: Q1.E, 12V_battery.-, ESP82266_module.GND
  N2: R1.Pin_1, R2.Pin_1, R3.Pin_1
  N3: 12V_battery.+, LED24.anode
